// Logisim project OpenCPU.circ as structural Verilog: 2 circuits, main circuit ALU
module ALU (
  input  [3:0] A,
  input  [3:0] A1,
  input  [3:0] B,
  input  [3:0] B1,
  input  [3:0] C,
  input  [3:0] C1,
  input  [2:0] codec,
  input  [3:0] D,
  input  [3:0] D1,
  output [3:0] output_pin
);

  wire [3:0] adder_1_out, divider_1_out, multiplier_1_out, subtractor_1_out;

  Adder #(.width(4)) adder_1 (.a(A), .b(A1), .out(adder_1_out));  // open: cin, cout
  Subtractor #(.width(4)) subtractor_1 (.a(B), .b(B1), .out(subtractor_1_out));  // open: bin, bout
  Multiplier #(.width(4)) multiplier_1 (.a(C), .b(C1), .out(multiplier_1_out));  // open: cin, cout
  Divider #(.width(4)) divider_1 (.a(D), .b(D1), .out(divider_1_out));  // open: upper, rem
  Multiplexer #(.select(3), .width(4)) multiplexer_1 (
    .in0(adder_1_out), .in1(subtractor_1_out), .in2(multiplier_1_out), .in3(divider_1_out), .out(output_pin),
    .sel(codec));  // open: in4, in5, in6, in7
endmodule

module CPU (
  input  [3:0] in_1,
  input  [3:0] in_2,
  input  [3:0] in_3,
  input  [3:0] in_4,
  input  [3:0] in_5,
  input  [3:0] in_6,
  input  [2:0] in_7,
  input  [3:0] in_8,
  input  [3:0] in_9
);

  wire button_1_out, clock_1_out;
  wire [3:0] alu_1_output_pin, register_1_q;

  ALU alu_1 (
    .A(in_1), .A1(in_2), .B(in_3), .B1(in_4), .C(in_5), .C1(in_6), .codec(in_7), .D(in_8), .D1(in_9),
    .output_pin(alu_1_output_pin));
  Register #(.width(4)) register_1 (
    .D(alu_1_output_pin), .en(clock_1_out), .clk(clock_1_out), .Q(register_1_q), .clr(button_1_out));
  Clock clock_1 (.out(clock_1_out));
  Button button_1 (.out(button_1_out));
  Hex_Digit_Display hex_digit_display_1 (.value(register_1_q));  // open: dp
endmodule
